# Fritzing sketch DC_motor_rpi (saved by Fritzing 0.9.1b)
breadboards: 1

parts:
  Raspberry_Pi1 = Raspberry Pi B+
  IC1 = L293D [package=THT]
  S1 = Pushbutton [package="[SMD]"]
  S3 = Pushbutton [package="[SMD]"]
  S4 = Pushbutton [package="[SMD]"]
  S5 = Pushbutton [package="[SMD]"]
  M1 = DC Motor  # not connected
  M2 = DC Motor  # not connected
  VCC1 = Battery block 9V

nets:
  N1: Raspberry_Pi1.GPIO17, IC1.In_1
  N2: Raspberry_Pi1.GPIO27, IC1.In_2
  N3: Raspberry_Pi1.GPIO21, S1.Pin_3, S1.Pin_4
  N4: Raspberry_Pi1.GPIO20, S5.Pin_3, S5.Pin_4
  N5: Raspberry_Pi1.GPIO12, S3.Pin_3, S3.Pin_4
  N6: Raspberry_Pi1.GND, IC1.0V, S1.Pin_1, S1.Pin_2, S3.Pin_1, S3.Pin_2, S4.Pin_1, S4.Pin_2, S5.Pin_1, S5.Pin_2, VCC1.-
  N7: Raspberry_Pi1.GPIO15, IC1.In_3
  N8: Raspberry_Pi1.GPIO14, IC1.In_4
  N9: Raspberry_Pi1.5V, IC1.Enable_2, IC1.+V
  N10: IC1.Out_1_(_Controlled_by_Enable_1_), IC1.Out_2_(_Controlled_by_Enable_1_)
  N11: IC1.Out_3_(_Controlled_by_Enable_2_), IC1.Out_4_(_Controlled_by_Enable_2_)
  N12: S4.Pin_3, S4.Pin_4

notes:
  9v battery for driving DC motor
