# Fritzing sketch Door alarm (saved by Fritzing 0.9.1b)
breadboards: 1

parts:
  U1 = HC-SR04 [chip_label=IC package="SIP (Single Inline) [THT]"]
  Part1 = Arduino Uno (Rev3) - ICSP
  J1 = Piezo Speaker

nets:
  VCC: U1.Vcc, Part1.5V
  N1: U1.Trig, Part1.D2
  N2: U1.Echo, Part1.D3_PWM
  GND: U1.GND, Part1.GND, J1.pin1
  N3: Part1.D12/MISO, J1.pin2

custom parts:
  HC-SR04: HC-SR04 ultrasound distance sensor
