# Fritzing sketch Line follower_rpi (saved by Fritzing 0.9.1b)
breadboards: 1

parts:
  Raspberry_Pi1 = Raspberry Pi B+
  IC1 = L293D [package=THT]
  M1 = DC Motor  # not connected
  M2 = DC Motor  # not connected
  VCC1 = Battery block 9V
  U1 = LMV324 [package=so014]
  R1 = Trimmer Potentiometer [maximum_resistance=10kΩ package=THT]
  IR1 = TSOP312.., 314.. [package=THT]
  LED1 = LEDs [package=led10mm]
  LED2 = smd LED [color="Red (633nm)" package="0603 [SMD]"]
  IR2 = TSOP312.., 314.. [package=THT]
  LED3 = smd LED [color="Red (633nm)" package="0603 [SMD]"]
  LED4 = LEDs [package=led10mm]

nets:
  N1: Raspberry_Pi1.GPIO17, IC1.In_1
  N2: Raspberry_Pi1.GPIO27, IC1.In_2
  N3: Raspberry_Pi1.GPIO21, U1.G$1_OUT, LED2.anode
  N4: Raspberry_Pi1.GPIO20, U1.G$2_OUT, LED3.cathode
  N5: Raspberry_Pi1.GPIO15, IC1.In_3
  N6: Raspberry_Pi1.GPIO14, IC1.In_4
  N7: Raspberry_Pi1.GND, IC1.0V, VCC1.-, U1.G$3_OUT, U1.G$3_-IN, U1.G$3_+IN, U1.G$1_-V, U1.G$4_+IN, U1.G$4_-IN, U1.G$4_OUT, R1.leg1, LED2.cathode
  N8: Raspberry_Pi1.5V, IC1.Enable_2, IC1.+V
  N9: IC1.Out_1_(_Controlled_by_Enable_1_), IC1.Out_2_(_Controlled_by_Enable_1_)
  N10: IC1.Out_3_(_Controlled_by_Enable_2_), IC1.Out_4_(_Controlled_by_Enable_2_)
  N11: U1.G$1_-IN, IR1.GND
  N12: U1.G$1_+IN, U1.G$2_+IN, R1.wiper
  N13: U1.G$1_+V, R1.leg2
  N14: U1.G$2_-IN, IR2.GND
  N15: IR1.Vs, LED1.A
  N16: IR1.Data, LED1.C
  N17: IR2.Vs, LED4.A
  N18: IR2.Data, LED4.C

notes:
  9v battery for driv ing DC motor
