# Fritzing sketch Servo_Rpi (saved by Fritzing 0.9.1b)
breadboards: 1

parts:
  Raspberry_Pi1 = Raspberry Pi B+
  J1 = Basic Servo
  C1 = Electrolytic Capacitor [capacitance=100µF package="200 mil [THT, electrolytic]"]
  R1 = Resistor [tolerance=±5% resistance=1k package=THT]

nets:
  N1: Raspberry_Pi1.GPIO21, R1.Pin_0
  GND: Raspberry_Pi1.GND, J1.gnd, C1.-
  5V: Raspberry_Pi1.5V, J1.vcc, C1.+
  N2: J1.pulse, R1.Pin_1

notes:
  Capacitor used to reduce vaibrations and 1k resistor to protect gpio from extra supply.
