# Fritzing sketch Stepper_Arduino (saved by Fritzing 0.9.1b)
breadboards: 1

parts:
  Part1 = Arduino Uno (Rev3) - ICSP
  M1 = Stepper Motor - Bipolar
  BAT1 = BC9VPC [package=bc9vpc]
  IC1 = L293D [package=THT]

nets:
  N1: Part1.D8, IC1.In_1
  N2: Part1.D9_PWM, IC1.In_2
  N3: Part1.D10_PWM/SS, IC1.In_4
  N4: Part1.GND, BAT1.V-, IC1.0V
  N5: Part1.5V, IC1.Enable_1, IC1.Enable_2, IC1.+V
  N6: M1.A, M1.C, IC1.Out_3_(_Controlled_by_Enable_2_), IC1.Out_4_(_Controlled_by_Enable_2_)
  N7: M1.B, M1.D, IC1.Out_1_(_Controlled_by_Enable_1_), IC1.Out_2_(_Controlled_by_Enable_1_)
  N8: BAT1.V+, IC1.+Vmotor

notes:
  to drive stepper motor external 9V battery supply.
