# Fritzing sketch Untitled Sketch (saved by Fritzing 0.9.1b)
breadboards: 1

parts:
  Part1 = Arduino Uno (Rev3)
  LED1 = LEDs [package=led10mm]
  S1 = Pushbutton [package="[THT]"]
  R1 = Resistor [tolerance=±5% resistance=220 package=THT]
  R2 = Resistor [tolerance=±5% resistance=220 package=THT]

nets:
  N1: Part1.GND, R1.Pin_0, R2.Pin_0
  N2: Part1.D5_PWM, Part1.5V, S1.Pin_3, S1.Pin_4
  N3: Part1.D7, LED1.C
  N4: LED1.A, R2.Pin_1
  N5: S1.Pin_1, S1.Pin_2, R1.Pin_1

// code stored in the sketch: Untitled.ino

