# Fritzing sketch lcd_2_Switch (saved by Fritzing 0.9.1b)
breadboards: 1

parts:
  Part1 = Arduino Uno (Rev3)
  LCD1 = LCD screen
  R1 = Trimmer Potentiometer [maximum_resistance=10kΩ package=THT]
  R2 = Resistor [tolerance=±5% resistance=220 package=THT]
  S1 = Pushbutton [package="[THT]"]
  S2 = Pushbutton [package="[THT]"]
  R3 = Resistor [tolerance=±5% resistance=220 package=THT]
  R4 = Resistor [tolerance=±5% resistance=220 package=THT]

nets:
  N1: Part1.D11_PWM/MOSI, LCD1.E
  N2: Part1.D12/MISO, LCD1.RS
  GND: Part1.GND, LCD1.VSS, LCD1.R/W, LCD1.LED-, R1.leg1, R3.Pin_0, R4.Pin_0
  N3: Part1.D2, LCD1.DB4
  N4: Part1.D3_PWM, LCD1.DB5
  N5: Part1.D4, LCD1.DB6
  N6: Part1.D5_PWM, LCD1.DB7
  5V: Part1.5V, LCD1.VDD, R1.leg2, R2.Pin_0
  N7: LCD1.V0, R1.wiper
  N8: LCD1.LED+, R2.Pin_1
  N9: S1.Pin_1, R3.Pin_1
  N10: S2.Pin_1, S2.Pin_2, R4.Pin_1
