# Fritzing sketch lcd_with_Arduino (saved by Fritzing 0.9.1b)
breadboards: 1

parts:
  LCD1 = LCD screen
  R1 = Trimmer Potentiometer [maximum_resistance=10kΩ package=THT]
  R2 = Resistor [tolerance=±5% resistance=220 package=THT]
  R3 = Trimmer Potentiometer [maximum_resistance=10kΩ package=THT]
  Raspberry_Pi1 = Raspberry Pi B+

nets:
  N1: LCD1.VSS, LCD1.R/W, LCD1.LED-, R1.leg2, R3.leg2
  N2: LCD1.VDD, R1.leg1, R2.Pin_0, R3.leg1
  N3: LCD1.V0, R1.wiper
  N4: LCD1.DB1, LCD1.DB6, Raspberry_Pi1.GPIO21
  N5: LCD1.LED+, R2.Pin_1
  N6: Raspberry_Pi1.GPIO27, Raspberry_Pi1.GPIO22
