# Fritzing sketch led danc (saved by Fritzing 0.9.1b)
breadboards: 1

parts:
  LED1 = LED - 3mm [color="Red (633nm)" package="3 mm [THT]"]
  LED2 = LED - 3mm [color="Red (633nm)" package="3 mm [THT]"]
  LED3 = LED - 3mm [color="Red (633nm)" package="3 mm [THT]"]
  LED4 = LED - 3mm [color="Red (633nm)" package="3 mm [THT]"]
  LED5 = LED - 3mm [color="Red (633nm)" package="3 mm [THT]"]
  LED6 = LED - 3mm [color="Red (633nm)" package="3 mm [THT]"]
  LED7 = LED - 3mm [color="Red (633nm)" package="3 mm [THT]"]
  LED8 = LED - 3mm [color="Red (633nm)" package="3 mm [THT]"]
  LED9 = LED - 3mm [color="Red (633nm)" package="3 mm [THT]"]
  LED10 = LED - 3mm [color="Red (633nm)" package="3 mm [THT]"]
  R1 = Resistor [tolerance=±5% resistance=220 package="1206 [SMD]"]
  R2 = Resistor [tolerance=±5% resistance=220 package=THT]
  R3 = Resistor [tolerance=±5% resistance=220 package=THT]
  R4 = Resistor [tolerance=±5% resistance=220 package=THT]
  R5 = Resistor [tolerance=±5% resistance=220 package=THT]
  R6 = Resistor [tolerance=±5% resistance=220 package=THT]
  R7 = Resistor [tolerance=±5% resistance=220 package=THT]
  R8 = Resistor [tolerance=±5% resistance=220 package=THT]
  R9 = Resistor [tolerance=±5% resistance=220 package=THT]
  R10 = Resistor [tolerance=±5% resistance=220 package=THT]
  Part1 = Arduino Uno (Rev3) - ICSP
  LED11 = LED - 3mm [color="Red (633nm)" package="3 mm [THT]"]
  R11 = Resistor [tolerance=±5% resistance=220 package="1206 [SMD]"]
  S1 = Momentary Switch [package=ksa_sealed_tac_switch]
  R12 = Resistor [tolerance=±5% resistance=220 package=THT]

nets:
  N1: LED1.cathode, LED2.cathode, LED3.cathode, LED4.cathode, LED5.cathode, LED6.cathode, LED7.cathode, LED8.cathode, LED9.cathode, LED10.cathode, Part1.GND, LED11.cathode, R12.Pin_0
  N2: LED1.anode, R2.Pin_0
  N3: LED2.anode, R9.Pin_0
  N4: LED3.anode, R8.Pin_0
  N5: LED4.anode, R10.Pin_0
  N6: LED5.anode, R3.Pin_0
  N7: LED6.anode, R4.Pin_0
  N8: LED7.anode, R7.Pin_0
  N9: LED8.anode, R5.Pin_0
  N10: LED9.anode, R6.Pin_0
  N11: LED10.anode, R1.Pin_0
  N12: R1.Pin_1, Part1.ICSP_MOSI, Part1.D11_PWM/MOSI
  N13: R2.Pin_1, Part1.D10_PWM/SS
  N14: R3.Pin_1, Part1.D6_PWM
  N15: R4.Pin_1, Part1.D5_PWM
  N16: R5.Pin_1, Part1.D3_PWM
  N17: R6.Pin_1, Part1.D2
  N18: R7.Pin_1, Part1.D4
  N19: R8.Pin_1, Part1.D8
  N20: R9.Pin_1, Part1.D9_PWM
  N21: R10.Pin_1, Part1.D7
  N22: Part1.ICSP_MISO, Part1.D12/MISO, R11.Pin_1
  N23: Part1.D1/TX, S1.4
  N24: LED11.anode, R11.Pin_0
  N25: S1.1, R12.Pin_1

notes:
  Yellow wire shows all negative leg of led connected commonly to ground.
