# Fritzing sketch servo_arduino (saved by Fritzing 0.9.1b)
breadboards: 1

parts:
  Part1 = Arduino Uno (Rev3) - ICSP
  J1 = Basic Servo
  R1 = Trimmer Potentiometer [maximum_resistance=10kΩ package=THT]
  C1 = Electrolytic Capacitor [capacitance=100µF package="200 mil [THT, electrolytic]"]

nets:
  GND: Part1.GND, J1.gnd, R1.leg1, C1.-
  N1: Part1.D9_PWM, J1.pulse
  N2: J1.vcc, R1.leg2, C1.+
